# Fritzing sketch pi_pwm_fan (saved by Fritzing 0.9.3b)

parts:
  J1 = Camdenboss CTB0158-4 [part_number=CTB0158-4 package=THT]
  Raspberry_Pi_1 = Raspberry Pi 3 [part_number=RPI-3-V1.2]

nets:
  N1: J1.pin1, Raspberry_Pi_1.GND
  N2: J1.pin2, Raspberry_Pi_1.5V
  N3: J1.terminal_4, Raspberry_Pi_1.GIPO18

notes:
  PWM Fan Bild Ersatz
  sw = GND
  ge = 5V+
  gn = Tacho (später)
  bl = PWM
